// Logisim project guess-the-number-x.circ as structural Verilog: 4 circuits, main circuit main
module main (
);

  wire A, A_jogando, A_venceu, and_2_out, and_3_out, and_4_out, and_5_out, and_6_out, \Avançar , \Avançar_A ,
       \Avançar_B , B, B_jogando, B_venceu, C_A, C_B, cfg, clk, comparator_1_eq, comparator_1_gt,
       comparator_1_lt, empate, Fim_A, Fim_B, fim_de_jogo, Iniciar, Jogando, Jogando_x, Jogando_y, m0, m0a_t,
       m0b_t, m1, m1a_t, m1b_t, or_6_out, or_7_out, PONTO, Reset, s0, s0a_t, s0b_t, s1, s1a_t, s1b_t,
       Soma_Certa, tunnel, tunnel_t, X_certo, Y_certo;
  wire [3:0] M0a, M0b, M1a, M1b, PA, PB, S0a, S0b, S1a, S1b, V_A, V_B, X_atual, Y_atual;
  wire [7:0] b_t, r;

  Clock clock_1 (.out(clk));
  LED led_1 (.in(tunnel));
  Hex_Digit_Display hex_digit_display_1 (.value(M0a));  // open: dp
  Hex_Digit_Display hex_digit_display_2 (.value(M1a));  // open: dp
  Button button (.out(m0a_t));
  Button button_2 (.out(m1a_t));
  Button button_3 (.out(A));
  or or_1 (s0, s0a_t, s0b_t);
  or or_2 (s1, s1a_t, s1b_t);
  or or_3 (m0, m0a_t, m0b_t);
  or or_4 (m1, m1a_t, m1b_t);
  S_R_Flip_Flop s_r_ff_1 (.S(Reset), .R(Iniciar), .Q(cfg), .preset(Reset), .reset(Iniciar));  // open: clk, Qn
  Hex_Digit_Display hex_digit_display_3 (.value(PA));  // open: dp
  Hex_Digit_Display hex_digit_display_4 (.value(S1a));  // open: dp
  Button button_4 (.out(s1a_t));
  Hex_Digit_Display hex_digit_display_5 (.value(V_A));  // open: dp
  Button button_5 (.out(C_A));
  LED led_2 (.in(A_jogando));
  or or_5 (\Avançar , \Avançar_A , \Avançar_B );
  not not_1 (Jogando, cfg);
  Hex_Digit_Display hex_digit_display_6 (.value(S0a));  // open: dp
  Button button_6 (.out(s0a_t));
  Button button_7 (.out(\Avançar_A ));
  LED led_3 (.in(X_certo));
  Counter #(.width(4), .max('hf)) counter_1 (
    .Q(V_A), .clk(A), .clr(or_6_out));  // open: load, D, count, carry, preset, down
  or or_6 (or_6_out, fim_de_jogo, Reset);
  Counter #(.width(4), .max('hf)) counter_2 (
    .Q(V_B), .clk(B), .clr(or_7_out));  // open: load, D, count, carry, preset, down
  or or_7 (or_7_out, fim_de_jogo, Reset);
  LED led_4 (.in(A_venceu));
  Hex_Digit_Display hex_digit_display_7 (.value(X_atual));  // open: dp
  LED led_5 (.in(Jogando_x));
  cronometro cronometro_1 (
    .clk(clk), .c_jogando(A_jogando), .cfg(cfg), .s0(s0), .s1(s1), .m0(m0), .m1(m1), .Fim_C(Fim_A),
    .S0c(S0a), .S1c(S1a), .M0c(M0a), .M1c(M1a), .reset(Reset));
  cronometro cronometro_2 (
    .clk(clk), .c_jogando(B_jogando), .cfg(cfg), .s0(s0), .s1(s1), .m0(m0), .m1(m1), .Fim_C(Fim_B),
    .S0c(S0b), .S1c(S1b), .M0c(M0b), .M1c(M1b), .reset(Reset));
  LED led_6 (.in(fim_de_jogo));
  LED led_7 (.in(empate));
  LED led_8 (.in(Soma_Certa));
  LED led_9 (.in(cfg));
  Button button_8 (.out(Iniciar));
  // RGBLed #(.multibit("true")) rgbled_1: pin names not known; wires that end beside it: r, b_t
  Hex_Digit_Display hex_digit_display_8 (.value(Y_atual));  // open: dp
  LED led_10 (.in(Jogando_y));
  Button button_9 (.out(Reset));
  LED led_11 (.in(B_venceu));
  LED led_12 (.in(Y_certo));
  and and_1 (PONTO, Soma_Certa, X_certo, Y_certo);
  and and_2 (and_2_out, PONTO, A_jogando);
  and and_3 (and_3_out, PONTO, B_jogando);
  core core_1 (
    .\Avançar (\Avançar ), .Jogando(Jogando), .Fim_A(Fim_A), .Fim_B(Fim_B), .C_A(C_A), .V_A(V_A),
    .Reset(Reset), .V_B(V_B), .C_B(C_B), .A_Jogando(A_jogando), .Jogando_X(Jogando_x), .B_Jogando(B_jogando),
    .Jogando_Y(Jogando_y), .r(r), .b(b_t), .Soma_Certa(Soma_Certa), .X_Certo(X_certo), .Y_Certo(Y_certo),
    .X_atual(X_atual), .Y_atual(Y_atual));
  Counter #(.width(4), .max('hf)) counter_3 (
    .Q(PA), .clk(and_2_out), .clr(Reset));  // open: load, D, count, carry, preset, down
  Counter #(.width(4), .max('hf)) counter_4 (
    .Q(PB), .clk(and_3_out), .clr(Reset));  // open: load, D, count, carry, preset, down
  Hex_Digit_Display hex_digit_display_9 (.value(M1b));  // open: dp
  Hex_Digit_Display hex_digit_display_10 (.value(M0b));  // open: dp
  Button button_10 (.out(m1b_t));
  Button button_11 (.out(m0b_t));
  Button button_12 (.out(B));
  LED led_13 (.in(tunnel_t));
  Hex_Digit_Display hex_digit_display_11 (.value(PB));  // open: dp
  Hex_Digit_Display hex_digit_display_12 (.value(S1b));  // open: dp
  Button button_13 (.out(s1b_t));
  Hex_Digit_Display hex_digit_display_13 (.value(V_B));  // open: dp
  Button button_14 (.out(C_B));
  LED led_14 (.in(B_jogando));
  Hex_Digit_Display hex_digit_display_14 (.value(S0b));  // open: dp
  Button button_15 (.out(s0b_t));
  Button button_16 (.out(\Avançar_B ));
  and and_4 (and_4_out, Fim_A, Fim_B);
  and and_5 (and_5_out, PA[0], PA[1], PA[2], PA[3]);
  and and_6 (and_6_out, PB[0], PB[1], PB[2], PB[3]);
  or or_8 (fim_de_jogo, and_4_out, and_5_out, and_6_out);
  Comparator #(.width(4)) comparator_1 (
    .a(PA), .b(PB), .gt(comparator_1_gt), .eq(comparator_1_eq), .lt(comparator_1_lt));
  and and_7 (A_venceu, comparator_1_gt, fim_de_jogo);
  and and_8 (empate, comparator_1_eq, fim_de_jogo);
  and and_9 (B_venceu, fim_de_jogo, comparator_1_lt);

  // Notes on the sheet:
  //   Tempo Geral
  //   Clock
  //   Estado
  //   jogador A
  //   PLACAR
  //   ⏱ CRONÔMETRO
  //   :
  //   Palpite
  //   Avançar
  //   Contador A
  //   Contador B
  //   A
  //   B
  //   Guess The Number EXTREME
  //   Pontuação
  //   jogador B
  //   PLACAR
  //   ⏱ CRONÔMETRO
  //   :
  //   Palpite
  //   Fim Do Jogo
endmodule

module cronometro (
  input  clk,
  input  c_jogando,
  input  cfg,
  input  s0,
  input  s1,
  input  m0,
  input  m1,
  input  reset,
  output Fim_C,
  output [3:0] S0c,
  output [3:0] S1c,
  output [3:0] M0c,
  output [3:0] M1c
);

  wire and_1_out, borrows0, borrows1, borrows2, comparator_1_eq, comparator_2_eq, comparator_3_eq,
       comparator_4_eq, multiplexer_1_out, multiplexer_2_out, multiplexer_3_out, multiplexer_4_out,
       not_1_out, not_2_out;

  not not_1 (not_1_out, Fim_C);
  not not_2 (not_2_out, cfg);
  and and_1 (and_1_out, not_1_out, clk, c_jogando, not_2_out);
  Multiplexer #(.enable("false")) multiplexer_1 (.in0(and_1_out), .in1(s0), .out(multiplexer_1_out), .sel(cfg));
  Multiplexer #(.enable("false")) multiplexer_2 (.in0(borrows0), .in1(s1), .out(multiplexer_2_out), .sel(cfg));
  Multiplexer #(.enable("false")) multiplexer_3 (.in0(borrows1), .in1(m0), .out(multiplexer_3_out), .sel(cfg));
  Multiplexer #(.enable("false")) multiplexer_4 (.in0(borrows2), .in1(m1), .out(multiplexer_4_out), .sel(cfg));
  Comparator #(.width(4)) comparator_1 (.a(4'b0000), .b(S0c), .eq(comparator_1_eq));  // open: gt, lt
  Comparator #(.width(4)) comparator_2 (.a(4'b0000), .b(S1c), .eq(comparator_2_eq));  // open: gt, lt
  Comparator #(.width(4)) comparator_3 (.a(4'b0000), .b(M0c), .eq(comparator_3_eq));  // open: gt, lt
  Comparator #(.width(4)) comparator_4 (.a(4'b0000), .b(M1c), .eq(comparator_4_eq));  // open: gt, lt
  Counter #(.width(4), .max('h9)) u_s0 (
    .Q(S0c), .carry(borrows0), .clk(multiplexer_1_out), .clr(reset), .down(1'b1));  // open: load, D, count, preset
  Counter #(.width(4), .max('h5), .trigger("falling")) u_s1 (
    .Q(S1c), .carry(borrows1), .clk(multiplexer_2_out), .clr(reset), .down(1'b1));  // open: load, D, count, preset
  Counter #(.width(4), .max('h9), .trigger("falling")) u_m0 (
    .Q(M0c), .carry(borrows2), .clk(multiplexer_3_out), .clr(reset), .down(1'b1));  // open: load, D, count, preset
  Counter #(.width(4), .max('h5), .trigger("falling")) u_m1 (
    .Q(M1c), .clk(multiplexer_4_out), .clr(reset), .down(1'b1));  // open: load, D, count, carry, preset
  and and_2 (Fim_C, comparator_1_eq, comparator_2_eq, comparator_3_eq, comparator_4_eq);
  Hex_Digit_Display hex_digit_display_1 (.value(M0c));  // open: dp
  Hex_Digit_Display hex_digit_display_2 (.value(M1c));  // open: dp
  Hex_Digit_Display hex_digit_display_3 (.value(S1c));  // open: dp
  Hex_Digit_Display hex_digit_display_4 (.value(S0c));  // open: dp

  // Other names for the same wires on the sheet: fim = Fim_C; modo = cfg; saidam0[3:0] = M0c; saidam1[3:0] = M1c;
  //   saidas0[3:0] = S0c; saidas1[3:0] = S1c

  // Notes on the sheet:
  //   clock
  //   0 jogo$1 config
  //   MUDAR NO MODO $CONFIG
  //   CONDICOES JOGO
  //   +CLOCK
  //   FIM
  //   SAIDAS
endmodule

module gnx (
  input  Confirmar,
  input  Novo_N,
  input  [3:0] X,
  input  [3:0] Y,
  output X_certo,
  output Y_certo,
  output Soma_certa,
  output [7:0] Vermelho,
  output [7:0] Azul
);

  wire and_4_out, and_5_out, comparator_1_eq, comparator_2_eq, comparator_3_eq, comparator_4_eq,
       comparator_4_gt, comparator_5_lt, not_1_out, or_1_out;
  wire [3:0] adder_1_out, adder_2_out;
  wire [4:0] multiplexer_1_out, subtractor_1_out, subtractor_2_out;
  wire [4:4] adder_1_cout, adder_2_cout;
  wire [7:0] random_1_out;

  Random random_1 (.clk(Novo_N), .out(random_1_out));  // open: next, clr
  Adder #(.width(4)) adder_1 (.a(Y), .b(X), .out(adder_1_out), .cout(adder_1_cout[4]));  // open: cin
  Adder #(.width(4)) adder_2 (
    .a(random_1_out[7:4]), .b(random_1_out[3:0]), .out(adder_2_out), .cout(adder_2_cout[4]));  // open: cin
  Comparator #(.width(4)) comparator_1 (.a(random_1_out[3:0]), .b(X), .eq(comparator_1_eq));  // open: gt, lt
  and and_1 (X_certo, comparator_1_eq, Confirmar);
  Comparator #(.width(4)) comparator_2 (.a(random_1_out[7:4]), .b(Y), .eq(comparator_2_eq));  // open: gt, lt
  and and_2 (Y_certo, comparator_2_eq, Confirmar);
  Comparator #(.width(5)) comparator_3 (
    .a({adder_2_cout[4], adder_2_out}), .b({adder_1_cout[4], adder_1_out}), .eq(comparator_3_eq));  // open: gt, lt
  and and_3 (Soma_certa, Confirmar, comparator_3_eq);
  Comparator #(.width(5)) comparator_4 (
    .a({adder_2_cout[4], adder_2_out}), .b({adder_1_cout[4], adder_1_out}), .gt(comparator_4_gt),
    .eq(comparator_4_eq));  // open: lt
  Subtractor #(.width(5)) subtractor_1 (
    .a({adder_2_cout[4], adder_2_out}), .b({adder_1_cout[4], adder_1_out}), .out(subtractor_1_out));  // open: bin, bout
  Subtractor #(.width(5)) subtractor_2 (
    .a({adder_1_cout[4], adder_1_out}), .b({adder_2_cout[4], adder_2_out}), .out(subtractor_2_out));  // open: bin, bout
  and and_4 (and_4_out, Confirmar, or_1_out);
  and and_5 (and_5_out, Confirmar, not_1_out);
  not not_1 (not_1_out, or_1_out);
  assign Vermelho = {{7{and_4_out}}, and_4_out};  // Bit_Extender bit_extender_1
  assign Azul = {{7{and_5_out}}, and_5_out};  // Bit_Extender bit_extender_2
  Multiplexer #(.width(5), .enable("false")) multiplexer_1 (
    .in0(subtractor_1_out), .in1(subtractor_2_out), .out(multiplexer_1_out), .sel(comparator_4_gt));
  Comparator #(.width(5)) comparator_5 (.a(multiplexer_1_out), .b(5'b00101), .lt(comparator_5_lt));  // open: gt, eq
  or or_1 (or_1_out, comparator_4_eq, comparator_5_lt);

  // Notes on the sheet:
  //   r
  //   b
endmodule

module core (
  input  \Avançar ,
  input  Jogando,
  input  Fim_A,
  input  Fim_B,
  input  C_A,
  input  [3:0] V_A,
  input  Reset,
  input  [3:0] V_B,
  input  C_B,
  output A_Jogando,
  output Jogando_X,
  output B_Jogando,
  output Jogando_Y,
  output [7:0] r,
  output [7:0] b,
  output Soma_Certa,
  output X_Certo,
  output Y_Certo,
  output [3:0] X_atual,
  output [3:0] Y_atual
);

  wire ACONFIRMADO, and_1_out, and_2_out, and_4_out, and_5_out, and_7_out, and_8_out, and_9_out, and_12_out,
       and_13_out, BCONFIRMADO, nor_1_out, not_1_out, not_2_out, not_3_out, or_1_out, or_2_out, or_3_out,
       or_4_out, or_5_out, or_6_out, or_7_out, or_8_out;
  wire [1:0] counter_1_q;
  wire [3:0] MUX;

  and and_1 (and_1_out, \Avançar , Jogando);
  or or_1 (or_1_out, counter_1_q[1], Fim_A);
  Multiplexer #(.width(4), .enable("false")) multiplexer_1 (.in0(V_A), .in1(V_B), .out(MUX), .sel(B_Jogando));
  Counter #(.width(2), .max('h3)) counter_1 (
    .Q(counter_1_q), .clk(and_1_out), .clr(Reset));  // open: load, D, count, carry, preset, down
  and and_2 (and_2_out, or_1_out, not_1_out);
  not not_1 (not_1_out, Fim_B);
  not not_2 (not_2_out, and_2_out);
  not not_3 (not_3_out, counter_1_q[0]);
  and and_3 (ACONFIRMADO, C_A, A_Jogando);
  and and_4 (and_4_out, C_B, B_Jogando);
  and and_5 (and_5_out, C_A, A_Jogando);
  and and_6 (BCONFIRMADO, C_B, B_Jogando);
  nor nor_1 (nor_1_out, counter_1_q[0], and_2_out);
  and and_7 (and_7_out, not_2_out, counter_1_q[0]);
  and and_8 (and_8_out, and_2_out, not_3_out);
  and and_9 (and_9_out, and_2_out, counter_1_q[0]);
  or or_2 (or_2_out, ACONFIRMADO, and_4_out);
  or or_3 (or_3_out, and_5_out, BCONFIRMADO);
  or or_4 (or_4_out, nor_1_out, and_7_out);
  and and_10 (A_Jogando, or_4_out, Jogando);
  or or_5 (or_5_out, and_8_out, and_9_out);
  and and_11 (B_Jogando, or_5_out, Jogando);
  and and_12 (and_12_out, or_2_out, Jogando_X);
  and and_13 (and_13_out, Jogando_Y, or_3_out);
  Register #(.width(4), .Select("low")) X (.D(MUX), .en(and_12_out), .Q(X_atual), .clr(Reset));  // open: clk
  Register #(.width(4), .Select("low")) Y (.D(MUX), .en(and_13_out), .Q(Y_atual), .clk(Reset), .clr(Reset));
  or or_6 (or_6_out, nor_1_out, and_8_out);
  or or_7 (or_7_out, and_7_out, and_9_out);
  and and_14 (Jogando_X, or_6_out, Jogando);
  and and_15 (Jogando_Y, or_7_out, Jogando);
  or or_8 (or_8_out, ACONFIRMADO, BCONFIRMADO);
  gnx gnx_1 (
    .Confirmar(or_8_out), .Novo_N(Reset), .X(X_atual), .Y(Y_atual), .Vermelho(r), .Azul(b),
    .X_certo(X_Certo), .Y_certo(Y_Certo), .Soma_certa(Soma_Certa));

  // Other names for the same wires on the sheet: AJOGANDO = A_Jogando; BJOGANDO = B_Jogando; CONFIRMAA = C_A;
  //   CONFIRMAB = C_B; JOGANDOX = Jogando_X; JOGANDOY = Jogando_Y; XATUAL[3:0] = X_atual; YATUAL[3:0] = Y_atual

  // Notes on the sheet:
  //   PALPITE
  //   LOGICA PARA FIM A
  //   A JOGANDO X
  //   A JOGANDO Y
  //   B JOGANDO X
  //   B JOGANDO Y
  //   CONDICAO X
  //   CONDICAO Y
  //   JOGANDO X
  //   JOGANDO Y
  //   Red
  //   Blue
endmodule
